# Fritzing sketch Schéma électronique (saved by Fritzing 0.9.5d)
breadboards: 1

parts:
  Composant1 = Arduino Mega 2560 (Rev3)
  Composant2 = Ludus ProtoShield Wireless
  U1 = XBEE-1 [package=xbee-1_lock]
  Composant3 = LIDAR-Lite
  Corps = Basic Servo
  LiDAR = Basic Servo

nets:
  5V: Composant1.5V, Composant3.5V, Corps.vcc, LiDAR.vcc
  GND: Composant1.GND, Composant3.GND, Corps.gnd, LiDAR.gnd
  N1: Composant2.9, U1.DTR
  N2: Composant2.11, U1.DIO4
  N3: Composant2.12, U1.CTS
  N4: Composant2.13, U1.DIO9
  N5: Composant2.16, U1.DIO5
  N6: Composant2.17, U1.RTS
  N7: Composant2.18, U1.DIO3
  N8: Composant2.DIO0, U1.DIO2
  N9: Composant2.D9, Corps.pulse
  N10: Composant2.D10, LiDAR.pulse
  N11: Composant2.SCL, Composant3.SCL
  N12: Composant2.SDA, Composant3.SDA

custom parts:
  LIDAR-Lite: PulsedLight LIDAR-Lite Sensor
